# Fritzing sketch greenhouse_schematic (saved by Fritzing 0.9.3b)
breadboards: 1

parts:
  RHT1 = Humidity and Temperature Sensor RHT03
  LDR = Photocell (LDR) [package=THT]
  R2 = Resistor [tolerance=±5% resistance=1k package="2010 [SMD]"]
  Part1 = Arduino Uno (Rev3)
  e-radionica1 = TCS230 Color Sensor [part_number=101209]
  Part2 = Soil Moisture Sensor
  Water_Level_Sensor1 = Water Level Sensor

nets:
  VCC: RHT1.Vcc, LDR.pin_0, Part1.5V, e-radionica1.Vcc, Part2.VCC, Water_Level_Sensor1.VCC
  N1: RHT1.Data-signal, Part1.D9_PWM
  GND: RHT1.GND_1, R2.Pin_1, Part1.GND, e-radionica1.Gnd, Part2.GND, Water_Level_Sensor1.GND
  N2: LDR.pin_1, R2.Pin_0, Part1.A0
  N3: Part1.A1, Part2.SIG
  N4: Part1.A2, Water_Level_Sensor1.SIG
  N5: Part1.D2, e-radionica1.S3
  N6: Part1.D3_PWM, e-radionica1.S2
  N7: Part1.D4, e-radionica1.OE, e-radionica1.Out
  N8: Part1.D5_PWM, e-radionica1.S1
  N9: Part1.D6_PWM, e-radionica1.S0

custom parts:
  TCS230 Color Sensor: TCS230
  Water Level Sensor: A water level sensor. This sensor operates at 3V to 5V. The Sig (signal) pin outputs an analogue signal that is in proportion to the amount of water in contact with the sensor.
